# Fritzing sketch potsch (saved by Fritzing 0.9.5d)

parts:
  Компонент1 = node32s
  Btn1 = Adafruit Push-button Power Switch Breakout [package=THT]
  Btn2 = Adafruit Push-button Power Switch Breakout [package=THT]
  A1 = MakerHawk optical endstop
  Pololu_A1 = Pololu A4988 [package=SO16]
  SW1 = DIP SWITCH [package=dipswitch-02]
  SW2 = DIP SWITCH [package=dipswitch-02]
  M1 = Stepper Motor - Bipolar
  Вход_питания1 = Camdenboss CTB0158-2 [package=THT]
  U2 = LM2596 step down module
  C4 = Electrolytic Capacitor [capacitance=10μF package="0605 [SMD, electrolytic]"]
  Pololu_A2 = Pololu A4988 [package=SO16]
  SW3 = DIP SWITCH [package=dipswitch-02]
  SW4 = DIP SWITCH [package=dipswitch-02]
  M2 = Stepper Motor - Bipolar
  C5 = Electrolytic Capacitor [capacitance=10μF package="0605 [SMD, electrolytic]"]
  Pololu_A3 = Pololu A4988 [package=SO16]
  SW5 = DIP SWITCH [package=dipswitch-02]
  SW6 = DIP SWITCH [package=dipswitch-02]
  M3 = Stepper Motor - Bipolar
  C6 = Electrolytic Capacitor [capacitance=10μF package="0605 [SMD, electrolytic]"]
  Pololu_A4 = Pololu A4988 [package=SO16]
  SW7 = DIP SWITCH [package=dipswitch-02]
  SW8 = DIP SWITCH [package=dipswitch-02]
  M4 = Stepper Motor - Bipolar
  C7 = Electrolytic Capacitor [capacitance=10μF package="0605 [SMD, electrolytic]"]
  J2 = Basic Servo

nets:
  N1: Компонент1.3.3V, Btn1.IN, Btn2.IN, A1.Pin_3
  N2: Компонент1.IO32, Btn2.OUT
  N3: Компонент1.IO33, Btn1.OUT
  N4: Компонент1.V_BATT, U2.OUT+
  VDD: Компонент1.5V, Pololu_A1.VDD, SW1.1, SW1.2, SW2.1, SW2.2, Pololu_A2.VDD, SW3.1, SW3.2, SW4.1, SW4.2, Pololu_A3.VDD, SW5.1, SW5.2, SW6.1, SW6.2, Pololu_A4.VDD, SW7.1, SW7.2, SW8.1, SW8.2, J2.vcc
  GND: Компонент1.GND, Btn1.GND, Btn2.GND, A1.Pin_2, Pololu_A1.GND, Вход_питания1.pin1, U2.IN-, U2.OUT-, C4.+, Pololu_A2.GND, C5.+, Pololu_A3.GND, C6.+, Pololu_A4.GND, C7.+, J2.gnd
  N5: Компонент1.IO23, A1.Pin_1
  N6: Компонент1.IO22, J2.pulse
  N7: Компонент1.IO19, Pololu_A4.STEP
  N8: Компонент1.IO18, Pololu_A4.DIR
  N9: Компонент1.IO5, Pololu_A3.STEP
  N10: Компонент1.IO17, Pololu_A3.DIR
  N11: Компонент1.IO16, Pololu_A2.STEP
  N12: Компонент1.IO4, Pololu_A2.DIR
  N13: Компонент1.IO2, Pololu_A1.STEP
  N14: Компонент1.IO15, Pololu_A1.DIR
  N15: Pololu_A1.MS1, SW2.4
  N16: Pololu_A1.MS2, SW2.3
  N17: Pololu_A1.MS3, SW1.4
  N18: Pololu_A1.RESET, Pololu_A1.SLEEP
  N19: Pololu_A1.1B, M1.C
  N20: Pololu_A1.1A, M1.A
  N21: Pololu_A1.2A, M1.B
  N22: Pololu_A1.2B, M1.D
  N23: Pololu_A1.VMOT, C4.-
  N24: Вход_питания1.pin2, U2.IN+
  N25: Pololu_A2.MS1, SW4.4
  N26: Pololu_A2.MS2, SW4.3
  N27: Pololu_A2.MS3, SW3.4
  N28: Pololu_A2.RESET, Pololu_A2.SLEEP
  N29: Pololu_A2.1B, M2.C
  N30: Pololu_A2.1A, M2.A
  N31: Pololu_A2.2A, M2.B
  N32: Pololu_A2.2B, M2.D
  N33: Pololu_A2.VMOT, C5.-
  N34: Pololu_A3.MS1, SW6.4
  N35: Pololu_A3.MS2, SW6.3
  N36: Pololu_A3.MS3, SW5.4
  N37: Pololu_A3.RESET, Pololu_A3.SLEEP
  N38: Pololu_A3.1B, M3.C
  N39: Pololu_A3.1A, M3.A
  N40: Pololu_A3.2A, M3.B
  N41: Pololu_A3.2B, M3.D
  N42: Pololu_A3.VMOT, C6.-
  N43: Pololu_A4.MS1, SW8.4
  N44: Pololu_A4.MS2, SW8.3
  N45: Pololu_A4.MS3, SW7.4
  N46: Pololu_A4.RESET, Pololu_A4.SLEEP
  N47: Pololu_A4.1B, M4.C
  N48: Pololu_A4.1A, M4.A
  N49: Pololu_A4.2A, M4.B
  N50: Pololu_A4.2B, M4.D
  N51: Pololu_A4.VMOT, C7.-

notes:
  шаговый двигатель для насоса
  сервопривод дозатора
  кнопка перехода в сервисный режим
  вход питания
  оптопара для парковки диска
  кнопка аварийной остановки

custom parts:
  MakerHawk optical endstop: MakerHawk optical endstop.
  LM2596 step down module: LM2596 DC-DC step down power supply module 3 A.
