# Fritzing sketch rfhugyiyghdgojhuyjtuy (saved by Fritzing 0.9.5d)

parts:
  Компонент1 = node32s
  Pololu_A1 = Pololu A4988 [package=SO16]
  SW1 = DIP SWITCH [package=dipswitch-02]
  SW2 = DIP SWITCH [package=dipswitch-02]
  M2 = Stepper Motor - Bipolar
  C1 = Electrolytic Capacitor [capacitance=10μF package="0605 [SMD, electrolytic]"]
  Pololu_A2 = Pololu A4988 [package=SO16]
  SW3 = DIP SWITCH [package=dipswitch-02]
  SW4 = DIP SWITCH [package=dipswitch-02]
  M3 = Stepper Motor - Bipolar
  C2 = Electrolytic Capacitor [capacitance=10μF package="0605 [SMD, electrolytic]"]
  Pololu_A3 = Pololu A4988 [package=SO16]
  SW5 = DIP SWITCH [package=dipswitch-02]
  SW6 = DIP SWITCH [package=dipswitch-02]
  M4 = Stepper Motor - Bipolar
  C3 = Electrolytic Capacitor [capacitance=10μF package="0605 [SMD, electrolytic]"]
  Pololu_A4 = Pololu A4988 [package=SO16]
  SW7 = DIP SWITCH [package=dipswitch-02]
  SW8 = DIP SWITCH [package=dipswitch-02]
  M5 = Stepper Motor - Bipolar
  C4 = Electrolytic Capacitor [capacitance=10μF package="0605 [SMD, electrolytic]"]
  Btn1 = Adafruit Push-button Power Switch Breakout [package=THT]
  Btn2 = Adafruit Push-button Power Switch Breakout [package=THT]
  J1 = Basic Servo
  A1 = MakerHawk optical endstop
  U1 = LM2596 step down module
  Вход_питания = Camdenboss CTB0158-2 [package=THT]

nets:
  N1: Компонент1.3.3V, Btn1.IN, Btn2.IN, A1.Pin_3
  N2: Компонент1.IO32, Btn1.OUT
  N3: Компонент1.IO33, Btn2.OUT
  N4: Компонент1.V_BATT, U1.OUT+
  VDD: Компонент1.5V, Pololu_A1.VDD, SW1.3, SW1.4, SW2.3, SW2.4, Pololu_A2.VDD, SW3.3, SW3.4, SW4.3, SW4.4, Pololu_A3.VDD, SW5.3, SW5.4, SW6.3, SW6.4, Pololu_A4.VDD, SW7.3, SW7.4, SW8.3, SW8.4, J1.vcc
  GND: Компонент1.GND, Pololu_A1.GND, C1.+, Pololu_A2.GND, C2.+, Pololu_A3.GND, C3.+, Pololu_A4.GND, C4.+, Btn1.GND, Btn2.GND, J1.gnd, A1.Pin_2, U1.IN-, U1.OUT-, Вход_питания.pin1
  N5: Компонент1.IO23, A1.Pin_1
  N6: Компонент1.IO22, J1.pulse
  N7: Компонент1.IO19, Pololu_A4.STEP
  N8: Компонент1.IO18, Pololu_A4.DIR
  N9: Компонент1.IO5, Pololu_A2.STEP
  N10: Компонент1.IO17, Pololu_A2.DIR
  N11: Компонент1.IO16, Pololu_A1.STEP
  N12: Компонент1.IO4, Pololu_A1.DIR
  N13: Компонент1.IO2, Pololu_A3.STEP
  N14: Компонент1.IO15, Pololu_A3.DIR
  N15: Pololu_A1.MS1, SW2.2
  N16: Pololu_A1.MS2, SW2.1
  N17: Pololu_A1.MS3, SW1.2
  N18: Pololu_A1.RESET, Pololu_A1.SLEEP
  N19: Pololu_A1.1B, M2.C
  N20: Pololu_A1.1A, M2.A
  N21: Pololu_A1.2A, M2.B
  N22: Pololu_A1.2B, M2.D
  N23: Pololu_A1.VMOT, C1.-
  N24: Pololu_A2.MS1, SW4.2
  N25: Pololu_A2.MS2, SW4.1
  N26: Pololu_A2.MS3, SW3.2
  N27: Pololu_A2.RESET, Pololu_A2.SLEEP
  N28: Pololu_A2.1B, M3.C
  N29: Pololu_A2.1A, M3.A
  N30: Pololu_A2.2A, M3.B
  N31: Pololu_A2.2B, M3.D
  N32: Pololu_A2.VMOT, C2.-
  N33: Pololu_A3.MS1, SW6.2
  N34: Pololu_A3.MS2, SW6.1
  N35: Pololu_A3.MS3, SW5.2
  N36: Pololu_A3.RESET, Pololu_A3.SLEEP
  N37: Pololu_A3.1B, M4.C
  N38: Pololu_A3.1A, M4.A
  N39: Pololu_A3.2A, M4.B
  N40: Pololu_A3.2B, M4.D
  N41: Pololu_A3.VMOT, C3.-
  N42: Pololu_A4.MS1, SW8.2
  N43: Pololu_A4.MS2, SW8.1
  N44: Pololu_A4.MS3, SW7.2
  N45: Pololu_A4.RESET, Pololu_A4.SLEEP
  N46: Pololu_A4.1B, M5.C
  N47: Pololu_A4.1A, M5.A
  N48: Pololu_A4.2A, M5.B
  N49: Pololu_A4.2B, M5.D
  N50: Pololu_A4.VMOT, C4.-
  N51: U1.IN+, Вход_питания.pin2

notes:
  вход питания
  шаговик диска
  шаговик насоса
  сервопривод дозатора
  аварийная кнопка
  сервискная кнопка

custom parts:
  MakerHawk optical endstop: MakerHawk optical endstop.
  LM2596 step down module: LM2596 DC-DC step down power supply module 3 A.
